// Logisim project ALU.circ as structural Verilog: 1 circuit, main circuit ALU
module ALU (
  input  [31:0] A,
  input  [31:0] B,
  input  [4:0] Shift,
  input  CarryIn,
  input  [3:0] Codop,
  output [31:0] S,
  output [3:0] Flags
);

  wire and_7_out, and_8_out, and_9_out, and_10_out, and_11_out, and_12_out, and_13_out, and_14_out,
       and_15_out, and_16_out, and_17_out, and_18_out, bitselector_2_out, bitselector_3_out,
       bitselector_4_out, bitselector_5_out, bitselector_6_out, bitselector_7_out, comparator_2_eq,
       comparator_3_eq, comparator_4_eq, comparator_4_lt, comparator_5_eq, comparator_5_lt, comparator_6_eq,
       comparator_7_eq, comparator_8_eq, comparator_8_lt, comparator_9_eq, comparator_9_lt, comparator_10_gt,
       comparator_10_lt, not_1_out, not_2_out, not_7_out, not_8_out, or_3_out, or_4_out, S1, S2, S3, S4,
       Signe;
  wire [4:0] subtractor_4_out, subtractor_5_out;
  wire [31:0] adder_1_out, adder_2_out, adder_3_out, and_1_out, and_2_out, and_3_out, and_4_out, and_5_out,
       and_6_out, multiplexer_2_out, multiplier_1_out, multiplier_2_out, negator_1_out, negator_2_out,
       not_3_out, not_4_out, not_5_out, not_6_out, or_1_out, or_2_out, shifter_1_out, shifter_2_out,
       shifter_3_out, shifter_4_out, shifter_5_out, shifter_6_out, shifter_7_out, shifter_8_out,
       subtractor_1_out, subtractor_2_out, subtractor_3_out, xor_1_out, xor_2_out;

  not not_1 (not_1_out, CarryIn);
  not not_2 (not_2_out, CarryIn);
  assign not_3_out = ~A;  // NOT_Gate not_3, 32 bits wide
  assign not_4_out = ~A;  // NOT_Gate not_4, 32 bits wide
  assign not_5_out = ~A;  // NOT_Gate not_5, 32 bits wide
  assign not_6_out = ~A;  // NOT_Gate not_6, 32 bits wide
  Adder #(.width(32)) adder_1 (.a(A), .b(B), .out(adder_1_out), .cin(CarryIn), .cout(S1));
  Subtractor #(.width(32)) subtractor_1 (.a(B), .b(A), .out(subtractor_1_out), .bin(not_1_out), .bout(S2));
  Negator #(.width(32)) negator_1 (.in(A), .out(negator_1_out));
  Adder #(.width(32)) adder_2 (.a(A), .b(B), .out(adder_2_out), .cin(CarryIn), .cout(S1));
  Subtractor #(.width(32)) subtractor_2 (.a(B), .b(A), .out(subtractor_2_out), .bin(not_2_out), .bout(S2));
  Adder #(.width(32)) adder_3 (.a(A), .b(B), .out(adder_3_out), .cout(S4));  // open: cin
  assign and_1_out = A & B;  // AND_Gate and_1, 32 bits wide
  assign xor_1_out = A ^ B;  // XOR_Gate xor_1, 32 bits wide
  Shifter #(.width(32)) shifter_1 (.in(B), .\dist (Shift), .out(shifter_1_out));
  Shifter #(.shift("lr"), .width(32)) shifter_2 (.in(B), .\dist (Shift), .out(shifter_2_out));
  Shifter #(.shift("ar"), .width(32)) shifter_3 (.in(B), .\dist (Shift), .out(shifter_3_out));
  Shifter #(.shift("rr"), .width(32)) shifter_4 (.in(B), .\dist (Shift), .out(shifter_4_out));
  assign and_2_out = A & B;  // AND_Gate and_2, 32 bits wide
  assign or_1_out = A | B;  // OR_Gate or_1, 32 bits wide
  Multiplier #(.width(32)) multiplier_1 (.a(A), .b(B), .out(multiplier_1_out));  // open: cin, cout
  assign and_3_out = not_3_out & B;  // AND_Gate and_3, 32 bits wide
  assign and_4_out = A & B;  // AND_Gate and_4, 32 bits wide
  assign xor_2_out = A ^ B;  // XOR_Gate xor_2, 32 bits wide
  Shifter #(.width(32)) shifter_5 (.in(B), .\dist (Shift), .out(shifter_5_out));
  Shifter #(.shift("lr"), .width(32)) shifter_6 (.in(B), .\dist (Shift), .out(shifter_6_out));
  Shifter #(.shift("ar"), .width(32)) shifter_7 (.in(B), .\dist (Shift), .out(shifter_7_out));
  Shifter #(.shift("rr"), .width(32)) shifter_8 (.in(B), .\dist (Shift), .out(shifter_8_out));
  assign and_5_out = A & B;  // AND_Gate and_5, 32 bits wide
  Negator #(.width(32)) negator_2 (.in(A), .out(negator_2_out));
  Subtractor #(.width(32)) subtractor_3 (.a(B), .b(A), .out(subtractor_3_out), .bout(S3));  // open: bin
  assign or_2_out = A | B;  // OR_Gate or_2, 32 bits wide
  Multiplier #(.width(32)) multiplier_2 (.a(A), .b(B), .out(multiplier_2_out));  // open: cin, cout
  assign and_6_out = not_5_out & B;  // AND_Gate and_6, 32 bits wide
  Multiplexer #(.enable("false"), .select(4), .width(32)) multiplexer_1 (
    .in0(and_1_out), .in1(xor_1_out), .in2(shifter_1_out), .in3(shifter_2_out), .in4(shifter_3_out),
    .in5(adder_1_out), .in6(subtractor_1_out), .in7(shifter_4_out), .in8(and_2_out), .in9(negator_1_out),
    .in10(B), .in11(B), .in12(or_1_out), .in13(multiplier_1_out), .in14(and_3_out), .in15(not_4_out),
    .out(S), .sel(Codop));
  Multiplexer #(.enable("false"), .select(4), .width(32)) multiplexer_2 (
    .in0(and_4_out), .in1(xor_2_out), .in2(shifter_5_out), .in3(shifter_6_out), .in4(shifter_7_out),
    .in5(adder_2_out), .in6(subtractor_2_out), .in7(shifter_8_out), .in8(and_5_out), .in9(negator_2_out),
    .in10(subtractor_3_out), .in11(adder_3_out), .in12(or_2_out), .in13(multiplier_2_out), .in14(and_6_out),
    .in15(not_6_out), .out(multiplexer_2_out), .sel(Codop));
  BitSelector #(.width(32)) bitselector_1 (.in(multiplexer_2_out), .out(Signe), .sel({5{1'b1}}));
  Comparator #(.width(32)) comparator_1 (
    .a(multiplexer_2_out), .b({32{1'b0}}), .eq(Flags[2]), .lt(Flags[3]));  // open: gt
  BitSelector #(.width(32)) bitselector_2 (.in(A), .out(bitselector_2_out), .sel({5{1'b1}}));
  BitSelector #(.width(32)) bitselector_3 (.in(B), .out(bitselector_3_out), .sel({5{1'b1}}));
  BitSelector #(.width(32)) bitselector_4 (.in(A), .out(bitselector_4_out), .sel({5{1'b1}}));
  BitSelector #(.width(32)) bitselector_5 (.in(B), .out(bitselector_5_out), .sel({5{1'b1}}));
  Subtractor #(.width(5)) subtractor_4 (.a({5{1'b0}}), .b(Shift), .out(subtractor_4_out));  // open: bin, bout
  Subtractor #(.width(5)) subtractor_5 (.a(Shift), .b(5'b00001), .out(subtractor_5_out));  // open: bin, bout
  Comparator #(.width(4)) comparator_2 (.a(Codop), .b(4'b0101), .eq(comparator_2_eq));  // open: gt, lt
  Comparator #(.width(4)) comparator_3 (.a(Codop), .b(4'b1011), .eq(comparator_3_eq));  // open: gt, lt
  Comparator #(.width(1)) comparator_4 (
    .a(bitselector_2_out), .b(1'b0), .eq(comparator_4_eq), .lt(comparator_4_lt));  // open: gt
  Comparator #(.width(1)) comparator_5 (
    .a(bitselector_3_out), .b(1'b0), .eq(comparator_5_eq), .lt(comparator_5_lt));  // open: gt
  Comparator #(.width(4)) comparator_6 (.a(Codop), .b(4'b0110), .eq(comparator_6_eq));  // open: gt, lt
  Comparator #(.width(4)) comparator_7 (.a(Codop), .b(4'b1010), .eq(comparator_7_eq));  // open: gt, lt
  Comparator #(.width(1)) comparator_8 (
    .a(bitselector_4_out), .b(1'b0), .eq(comparator_8_eq), .lt(comparator_8_lt));  // open: gt
  Comparator #(.width(1)) comparator_9 (
    .a(bitselector_5_out), .b(1'b0), .eq(comparator_9_eq), .lt(comparator_9_lt));  // open: gt
  BitSelector #(.width(32)) bitselector_6 (.in(B), .out(bitselector_6_out), .sel(subtractor_4_out));
  BitSelector #(.width(32)) bitselector_7 (.in(B), .out(bitselector_7_out), .sel(subtractor_5_out));
  or or_3 (or_3_out, comparator_2_eq, comparator_3_eq);
  and and_7 (and_7_out, comparator_4_eq, comparator_5_eq);
  and and_8 (and_8_out, comparator_4_lt, comparator_5_lt);
  or or_4 (or_4_out, comparator_6_eq, comparator_7_eq);
  and and_9 (and_9_out, comparator_8_lt, comparator_9_eq);
  and and_10 (and_10_out, comparator_8_eq, comparator_9_lt);
  not not_7 (not_7_out, S2);
  and and_11 (and_11_out, or_4_out, and_9_out);
  and and_12 (and_12_out, and_10_out, or_4_out);
  not not_8 (not_8_out, S3);
  and and_13 (and_13_out, or_3_out, and_7_out);
  and and_14 (and_14_out, and_8_out, or_3_out);
  Comparator #(.width(1)) comparator_10 (
    .a(Signe), .b(1'b0), .gt(comparator_10_gt), .lt(comparator_10_lt));  // open: eq
  Multiplexer #(.enable("false"), .select(4)) multiplexer_3 (
    .in0(1'b0), .in1(1'b0), .in2(bitselector_6_out), .in3(bitselector_7_out), .in4(bitselector_7_out),
    .in5(S1), .in6(not_7_out), .in7(1'b0), .in8(1'b0), .in9(1'b0), .in10(not_8_out), .in11(S4), .in12(1'b0),
    .in13(1'b0), .in14(1'b0), .in15(1'b0), .out(Flags[1]), .sel(Codop));
  and and_15 (and_15_out, comparator_10_lt, and_13_out);
  and and_16 (and_16_out, and_14_out, comparator_10_gt);
  and and_17 (and_17_out, comparator_10_lt, and_11_out);
  and and_18 (and_18_out, and_12_out, comparator_10_gt);
  or or_5 (Flags[0], and_15_out, and_16_out, and_17_out, and_18_out);

  // Other names for the same wires on the sheet: Overflow = Flags[0]; CarryOut = Flags[1]

  // Notes on the sheet:
  //   Note: for ROR, C = N
  //   Note 2: assume that shift > 0 for LSL and LSR
endmodule
