// Logisim project Ctl_Load_Store.circ as structural Verilog: 1 circuit, main circuit Load_Store
module Load_Store (
  input  [15:0] Instruction,
  input  Clk,
  input  Reset,
  input  Enable,
  input  [31:0] Stack_Pointer,
  output Store,
  output Load,
  output PC_Hold,
  output [2:0] Rmd,
  output [31:0] RAM_Addr
);

  wire and_1_out, bitselector_1_out, d_ff_1_q, d_ff_1_qn, not_1_out, not_2_out, not_3_out;
  wire [2:0] bitselector_4_out;
  wire [7:0] bitselector_5_out;
  wire [31:0] adder_1_out, bit_extender_1_out;

  BitSelector #(.width(16)) bitselector_1 (.in(Instruction), .out(bitselector_1_out), .sel(4'b1011));
  BitSelector #(.width(16)) bitselector_2 (.in(Instruction), .out(bitselector_4_out[2]), .sel(4'b1010));
  BitSelector #(.width(16)) bitselector_3 (.in(Instruction), .out(bitselector_4_out[1]), .sel(4'b1001));
  BitSelector #(.width(16)) bitselector_4 (.in(Instruction), .out(bitselector_4_out[0]), .sel(4'b1000));
  BitSelector #(.group(8), .width(16)) bitselector_5 (.in(Instruction), .out(bitselector_5_out), .sel(1'b0));
  assign bit_extender_1_out = {{24{1'b0}}, bitselector_5_out};  // Bit_Extender bit_extender_1
  not not_1 (not_1_out, d_ff_1_q);
  and and_1 (and_1_out, not_1_out, Enable);
  D_Flip_Flop d_ff_1 (.D(and_1_out), .clk(Clk), .Q(d_ff_1_q), .Qn(d_ff_1_qn), .reset(Reset));  // open: preset
  Adder #(.width(32)) adder_1 (.a(Stack_Pointer), .b(bit_extender_1_out), .out(adder_1_out));  // open: cin, cout
  not not_2 (not_2_out, bitselector_1_out);
  and and_2 (Store, not_2_out, Enable);
  and and_3 (Load, Enable, bitselector_1_out, not_3_out);
  not not_3 (not_3_out, d_ff_1_qn);
  and and_4 (PC_Hold, d_ff_1_q, Enable);
  Pull_Resistor pull_resistor_1 (.node(Rmd));
  assign Rmd = Enable ? bitselector_4_out : 3'bz;  // Controlled_Buffer controlled_buffer_1
  assign RAM_Addr = Enable ? adder_1_out : 32'bz;  // Controlled_Buffer controlled_buffer_2
  Pull_Resistor pull_resistor_2 (.node(RAM_Addr));

  // Notes on the sheet:
  //   Instruction: pull=down
  //   Delay load and hold PC for 1 cycle for the RAM to send out requested data 
endmodule
