// Logisim project Ctl_SP_Address.circ as structural Verilog: 1 circuit, main circuit SP_Address
module SP_Address (
  input  Enable,
  input  [31:0] Stack_Pointer,
  input  [15:0] Instruction,
  output [31:0] New_Stack_Pointer,
  output Write_Enable
);

  wire ADDorSUB;
  wire [6:0] bitselector_2_out;
  wire [31:0] adder_1_out, multiplexer_1_out, NEW_VAL, subtractor_1_out;

  Adder #(.width(32)) adder_1 (.a(NEW_VAL), .b(Stack_Pointer), .out(adder_1_out));  // open: cin, cout
  Subtractor #(.width(32)) subtractor_1 (.a(Stack_Pointer), .b(NEW_VAL), .out(subtractor_1_out));  // open: bin, bout
  BitSelector #(.width(16)) bitselector_1 (.in(Instruction), .out(ADDorSUB), .sel(4'b0111));
  BitSelector #(.group(7), .width(16)) bitselector_2 (.in(Instruction), .out(bitselector_2_out), .sel(2'b00));
  Multiplexer #(.enable("false"), .width(32)) multiplexer_1 (
    .in0(adder_1_out), .in1(subtractor_1_out), .out(multiplexer_1_out), .sel(ADDorSUB));
  assign NEW_VAL = {{25{1'b0}}, bitselector_2_out};  // Bit_Extender bit_extender_1
  Multiplexer #(.enable("false"), .width(32)) multiplexer_2 (
    .in0({32{1'b0}}), .in1(multiplexer_1_out), .out(New_Stack_Pointer), .sel(Enable));

  assign Write_Enable = Enable;

  // Other names for the same wires on the sheet: Mem[31:0] = Stack_Pointer

  // Notes on the sheet:
  //   Pull output low on Enable = 0
endmodule
