// Logisim project Ctl_Opcode_Decoder.circ as structural Verilog: 1 circuit, main circuit Opcode_Decoder
module Opcode_Decoder (
  input  [5:0] Opcode,
  output [1:0] out_2,
  output Shift,
  output Data_Processing,
  output [5:0] out_5,
  output [3:0] out_6,
  output Load_Store,
  output [3:0] out_8,
  output [3:0] out_9,
  output SP_Address,
  output [3:0] out_11,
  output [3:0] out_12,
  output Conditional,
  output [3:0] out_14
);

  BitSelector #(.group(2), .width(6)) bitselector_1 (.in(Opcode), .out(out_2), .sel(2'b10));
  BitSelector #(.group(2), .width(6)) bitselector_2 (.in(Opcode), .out(out_6[1:0]), .sel(2'b01));
  BitSelector #(.group(2), .width(6)) bitselector_3 (.in(Opcode), .out(out_6[3:2]), .sel(2'b10));
  BitSelector #(.group(2), .width(6)) bitselector_4 (.in(Opcode), .out(out_9[1:0]), .sel(2'b01));
  BitSelector #(.group(2), .width(6)) bitselector_5 (.in(Opcode), .out(out_9[3:2]), .sel(2'b10));
  BitSelector #(.group(2), .width(6)) bitselector_6 (.in(Opcode), .out(out_12[1:0]), .sel(2'b01));
  BitSelector #(.group(2), .width(6)) bitselector_7 (.in(Opcode), .out(out_12[3:2]), .sel(2'b10));
  Comparator #(.width(2)) comparator_1 (.a(out_2), .b(2'b00), .eq(Shift));  // open: gt, lt
  Comparator #(.width(6)) comparator_2 (.a(Opcode), .b(6'b010000), .eq(Data_Processing));  // open: gt, lt
  Comparator #(.width(4)) comparator_3 (.a(out_6), .b(4'b1001), .eq(Load_Store));  // open: gt, lt
  Comparator #(.width(4)) comparator_4 (.a(out_9), .b(4'b1011), .eq(SP_Address));  // open: gt, lt
  Comparator #(.width(4)) comparator_5 (.a(out_12), .b(4'b1101), .eq(Conditional));  // open: gt, lt

  assign out_5 = 6'b010000;
  assign out_8 = 4'b1001;
  assign out_11 = 4'b1011;
  assign out_14 = 4'b1101;

  // Notes on the sheet:
  //   Shift, add, sub, mov
  //   Data Processing
  //   Load/Store
  //   SP Address
  //   Conditional branch
endmodule
