// Logisim project ALU.circ as structural Verilog: 1 circuit, main circuit ALU
module ALU (
  input  [31:0] A,
  input  [31:0] B,
  input  [4:0] Shift,
  input  [3:0] Codop,
  input  CarryIn,
  output [31:0] S,
  output [3:0] Flags
);

  wire A_SIGN, adder_1_cout, adder_2_cout, and_4_out, and_5_out, B_SIGN, bitselector_4_out,
       bitselector_5_out, C_LSL, C_LSR_ASR, C_ROR, not_1_out, not_3_out, not_4_out, subtractor_1_bout,
       subtractor_2_bout, xnor_1_out, xnor_2_out, xor_2_out, xor_3_out;
  wire [4:0] negator_2_out, subtractor_3_out;
  wire [31:0] adder_1_out, and_1_out, and_3_out, F_CMN, F_CMP, F_TST, multiplexer_3_out, multiplier_1_out,
       negator_1_out, not_2_out, or_1_out, r, shifter_1_out, shifter_2_out, shifter_3_out, subtractor_1_out,
       xor_1_out;

  not not_1 (not_1_out, CarryIn);
  assign and_1_out = A & B;  // AND_Gate and_1, 32 bits wide
  assign xor_1_out = A ^ B;  // XOR_Gate xor_1, 32 bits wide
  Shifter #(.width(32)) shifter_1 (.in(B), .\dist (Shift), .out(shifter_1_out));
  Shifter #(.shift("lr"), .width(32)) shifter_2 (.in(B), .\dist (Shift), .out(shifter_2_out));
  Shifter #(.shift("ar"), .width(32)) shifter_3 (.in(B), .\dist (Shift), .out(shifter_3_out));
  Adder #(.width(32)) adder_1 (.a(A), .b(B), .out(adder_1_out), .cin(CarryIn), .cout(adder_1_cout));
  Subtractor #(.width(32)) subtractor_1 (
    .a(B), .b(A), .out(subtractor_1_out), .bin(not_1_out), .bout(subtractor_1_bout));
  Shifter #(.shift("rr"), .width(32)) shifter_4 (.in(B), .\dist (Shift), .out(r));
  assign F_TST = A & B;  // AND_Gate and_2, 32 bits wide
  Negator #(.width(32)) negator_1 (.in(A), .out(negator_1_out));
  Subtractor #(.width(32)) subtractor_2 (.a(B), .b(A), .out(F_CMP), .bin(1'b0), .bout(subtractor_2_bout));
  Adder #(.width(32)) adder_2 (.a(A), .b(B), .out(F_CMN), .cin(1'b0), .cout(adder_2_cout));
  assign or_1_out = A | B;  // OR_Gate or_1, 32 bits wide
  Multiplier #(.width(32)) multiplier_1 (.a(A), .b(B), .out(multiplier_1_out), .cin({32{1'b0}}));  // open: cout
  assign and_3_out = B & ~A;  // AND_Gate and_3, 32 bits wide
  assign not_2_out = ~A;  // NOT_Gate not_2, 32 bits wide
  not not_3 (not_3_out, subtractor_1_bout);
  not not_4 (not_4_out, subtractor_2_bout);
  Negator #(.width(5)) negator_2 (.in(Shift), .out(negator_2_out));
  Subtractor #(.width(5)) subtractor_3 (.a(Shift), .b(5'b00001), .out(subtractor_3_out));  // open: bin, bout
  Multiplexer #(.enable("false"), .select(4), .width(32)) multiplexer_1 (
    .in0(and_1_out), .in1(xor_1_out), .in2(shifter_1_out), .in3(shifter_2_out), .in4(shifter_3_out),
    .in5(adder_1_out), .in6(subtractor_1_out), .in7(r), .in8(B), .in9(negator_1_out), .in10(B), .in11(B),
    .in12(or_1_out), .in13(multiplier_1_out), .in14(and_3_out), .in15(not_2_out), .out(S), .sel(Codop));
  Multiplexer #(.enable("false"), .select(4)) multiplexer_2 (
    .in0(1'b0), .in1(1'b0), .in2(C_LSL), .in3(C_LSR_ASR), .in4(C_LSR_ASR), .in5(adder_1_cout),
    .in6(not_3_out), .in7(C_ROR), .in8(1'b0), .in9(1'b0), .in10(not_4_out), .in11(adder_2_cout), .in12(1'b0),
    .in13(1'b0), .in14(1'b0), .in15(1'b0), .out(Flags[1]), .sel(Codop));
  BitSelector #(.width(32)) bitselector_1 (.in(B), .out(C_LSL), .sel(negator_2_out));
  BitSelector #(.width(32)) bitselector_2 (.in(B), .out(C_LSR_ASR), .sel(subtractor_3_out));
  BitSelector #(.width(32)) bitselector_3 (.in(r), .out(C_ROR), .sel({5{1'b1}}));
  BitSelector #(.width(32)) bitselector_4 (.in(S), .out(bitselector_4_out), .sel({5{1'b1}}));
  Multiplexer #(.enable("false"), .select(4), .width(32)) multiplexer_3 (
    .in0(S), .in1(S), .in2(S), .in3(S), .in4(S), .in5(S), .in6(S), .in7(S), .in8(F_TST), .in9(S),
    .in10(F_CMP), .in11(F_CMN), .in12(S), .in13(S), .in14(S), .in15(S), .out(multiplexer_3_out), .sel(Codop));
  BitSelector #(.width(32)) bitselector_5 (.in(F_CMN), .out(bitselector_5_out), .sel({5{1'b1}}));
  xor xor_2 (xor_2_out, B_SIGN, bitselector_4_out);
  and and_4 (and_4_out, xor_2_out, xnor_1_out);
  xnor xnor_1 (xnor_1_out, A_SIGN, B_SIGN);
  xnor xnor_2 (xnor_2_out, A_SIGN, B_SIGN);
  xor xor_3 (xor_3_out, B_SIGN, bitselector_5_out);
  Comparator #(.width(32)) comparator_1 (
    .a(multiplexer_3_out), .b({32{1'b0}}), .eq(Flags[2]), .lt(Flags[3]));  // open: gt
  and and_5 (and_5_out, xnor_2_out, xor_3_out);
  BitSelector #(.width(32)) bitselector_6 (.in(B), .out(B_SIGN), .sel({5{1'b1}}));
  BitSelector #(.width(32)) bitselector_7 (.in(A), .out(A_SIGN), .sel({5{1'b1}}));
  Multiplexer #(.enable("false"), .select(4)) multiplexer_4 (
    .in0(1'b0), .in1(1'b0), .in2(1'b0), .in3(1'b0), .in4(1'b0), .in5(and_4_out), .in6(1'b0), .in7(1'b0),
    .in8(1'b0), .in9(1'b0), .in10(1'b0), .in11(and_5_out), .in12(1'b0), .in13(1'b0), .in14(1'b0),
    .in15(1'b0), .out(Flags[0]), .sel(Codop));

  // Other names for the same wires on the sheet: V = Flags[0]; C = Flags[1]; Z = Flags[2]; N = Flags[3]

  // Notes on the sheet:
  //   Note: for ROR, C = N
  //   Note 2: assume that shift > 0 for LSL and LSR
endmodule
