// Logisim project Ctl_Conditional.circ as structural Verilog: 2 circuits, main circuit Conditional
module Conditional (
  input  [15:0] Instruction,
  input  Z,
  input  C,
  input  N,
  input  V,
  input  Enable,
  output [10:0] Offset,
  output Verified
);

  wire conditions_1_verified;

  Conditions conditions_1 (
    .b8(Instruction[8]), .b9(Instruction[9]), .b10(Instruction[10]), .b11(Instruction[11]), .Z(Z), .C(C),
    .V(N), .N(V), .Verified(conditions_1_verified));
  Multiplexer #(.enable("false"), .width(11)) multiplexer_1 (
    .in0({11{1'b0}}), .in1(Instruction[10:0]), .out(Offset), .sel(Verified));
  and and_1 (Verified, conditions_1_verified, Enable);
endmodule

module Conditions (
  input  b8,
  input  b9,
  input  b10,
  input  b11,
  input  Z,
  input  C,
  input  V,
  input  N,
  output Verified
);

  wire AL, and_9_out, and_10_out, and_11_out, and_12_out, and_13_out, and_19_out, CC_LO, CS_HS, EQ, FALSE,
       GE, GT, HI, LE, LS, LT, MI, NE, not_1_out, not_2_out, not_3_out, not_4_out, not_5_out, not_6_out,
       not_7_out, not_8_out, not_9_out, not_10_out, not_11_out, not_12_out, not_13_out, not_14_out,
       not_15_out, not_16_out, not_17_out, not_18_out, not_19_out, not_20_out, not_21_out, not_22_out,
       not_23_out, not_24_out, not_25_out, not_26_out, not_27_out, not_28_out, not_29_out, not_30_out,
       not_31_out, not_32_out, not_33_out, not_34_out, not_35_out, not_36_out, not_37_out, not_38_out,
       not_39_out, not_40_out, not_41_out, not_42_out, not_43_out, not_44_out, not_45_out, not_46_out,
       not_47_out, not_48_out, not_49_out, or_1_out, or_2_out, or_3_out, or_4_out, or_5_out, or_6_out,
       or_7_out, or_8_out, or_9_out, PL, VC, VS;

  not not_1 (not_1_out, b8);
  not not_2 (not_2_out, b9);
  not not_3 (not_3_out, b10);
  not not_4 (not_4_out, b11);
  not not_5 (not_5_out, b9);
  not not_6 (not_6_out, b10);
  not not_7 (not_7_out, b11);
  not not_8 (not_8_out, Z);
  not not_9 (not_9_out, b8);
  not not_10 (not_10_out, b10);
  not not_11 (not_11_out, b11);
  not not_12 (not_12_out, b10);
  not not_13 (not_13_out, b11);
  not not_14 (not_14_out, C);
  not not_15 (not_15_out, b8);
  not not_16 (not_16_out, b9);
  not not_17 (not_17_out, b11);
  not not_18 (not_18_out, b9);
  not not_19 (not_19_out, b11);
  not not_20 (not_20_out, V);
  not not_21 (not_21_out, b8);
  not not_22 (not_22_out, b11);
  not not_23 (not_23_out, b11);
  not not_24 (not_24_out, N);
  and and_1 (EQ, not_1_out, not_2_out, not_3_out, not_4_out, Z);
  and and_2 (NE, b8, not_5_out, not_6_out, not_7_out, not_8_out);
  and and_3 (CS_HS, not_9_out, b9, not_10_out, not_11_out, C);
  and and_4 (CC_LO, b8, b9, not_12_out, not_13_out, not_14_out);
  and and_5 (MI, not_15_out, not_16_out, b10, not_17_out, V);
  and and_6 (PL, b8, not_18_out, b10, not_19_out, not_20_out);
  and and_7 (VS, not_21_out, b9, b10, not_22_out, N);
  and and_8 (VC, b8, b9, b10, not_23_out, not_24_out);
  not not_25 (not_25_out, b8);
  not not_26 (not_26_out, b9);
  not not_27 (not_27_out, b10);
  and and_9 (and_9_out, C, not_28_out);
  not not_28 (not_28_out, Z);
  not not_29 (not_29_out, b8);
  not not_30 (not_30_out, b9);
  not not_31 (not_31_out, b10);
  not not_32 (not_32_out, b11);
  not not_33 (not_33_out, C);
  and and_10 (and_10_out, not_33_out, Z);
  not not_34 (not_34_out, b9);
  not not_35 (not_35_out, b11);
  or or_1 (or_1_out, V, not_36_out);
  not not_36 (not_36_out, N);
  not not_37 (not_37_out, V);
  or or_2 (or_2_out, not_37_out, N);
  not not_38 (not_38_out, b10);
  or or_3 (or_3_out, V, N);
  not not_39 (not_39_out, V);
  or or_4 (or_4_out, not_39_out, not_40_out);
  not not_40 (not_40_out, N);
  not not_41 (not_41_out, b8);
  not not_42 (not_42_out, b9);
  or or_5 (or_5_out, V, not_43_out);
  not not_43 (not_43_out, N);
  not not_44 (not_44_out, V);
  or or_6 (or_6_out, not_44_out, N);
  not not_45 (not_45_out, Z);
  and and_11 (and_11_out, or_1_out, or_2_out);
  and and_12 (and_12_out, or_3_out, or_4_out);
  and and_13 (and_13_out, or_5_out, or_6_out);
  and and_14 (HI, not_25_out, not_26_out, not_27_out, b11, and_9_out);
  and and_15 (LS, not_29_out, not_30_out, not_31_out, not_32_out, and_10_out);
  and and_16 (GE, b8, not_34_out, b10, not_35_out, and_11_out);
  and and_17 (LT, b8, b9, not_38_out, b11, and_12_out);
  and and_18 (GT, not_41_out, not_42_out, b11, and_13_out, not_45_out);
  not not_46 (not_46_out, b9);
  not not_47 (not_47_out, V);
  not not_48 (not_48_out, N);
  not not_49 (not_49_out, b8);
  or or_7 (or_7_out, V, N);
  and and_19 (and_19_out, or_7_out, or_8_out);
  or or_8 (or_8_out, not_47_out, not_48_out);
  or or_9 (or_9_out, and_19_out, Z);
  and and_20 (LE, b8, not_46_out, b10, b11, or_9_out);
  and and_21 (AL, not_49_out, b9, b10, b11);
  and and_22 (FALSE, b8, b9, b10, b11);
  or or_10 (Verified, EQ, NE, CS_HS, CC_LO, MI, PL, VS, VC, HI, LS, GE, LT, GT, LE, AL, FALSE);

  // Other names for the same wires on the sheet: N_t = V; V_t = N
endmodule
