// Logisim project Ctl_Data_Processing.circ as structural Verilog: 2 circuits, main circuit Data_Processing
module Data_Processing (
  input  Enable,
  input  [15:0] Instruction,
  output [3:0] ALU_Opcode,
  output [3:0] Flags_Update_Mask,
  output [2:0] Rd,
  output [2:0] Rn,
  output [2:0] Rm
);

  wire ADC, ANDS, ASR, BIC, CMN, CMP, EOR, inv, LSL, LSR, MUL, MVN, not_1_out, not_2_out, not_3_out,
       not_4_out, not_5_out, not_6_out, not_7_out, not_8_out, not_9_out, not_10_out, not_11_out, not_12_out,
       not_13_out, not_14_out, not_15_out, not_16_out, not_17_out, not_18_out, not_19_out, not_20_out,
       not_21_out, not_22_out, not_23_out, not_24_out, not_25_out, not_26_out, not_27_out, not_28_out,
       not_29_out, not_30_out, not_31_out, not_32_out, ORR, RORS, RSB, SBC, TST;
  wire [2:0] multiplexer_3_out, multiplexer_4_out, rminv, rninv;
  wire [3:0] res_flag;

  not not_1 (not_1_out, Instruction[7]);
  and and_1 (MUL, Instruction[6], not_1_out, Instruction[8], Instruction[9]);
  not not_2 (not_2_out, Instruction[6]);
  not not_3 (not_3_out, Instruction[7]);
  not not_4 (not_4_out, Instruction[8]);
  not not_5 (not_5_out, Instruction[9]);
  not not_6 (not_6_out, Instruction[7]);
  not not_7 (not_7_out, Instruction[8]);
  not not_8 (not_8_out, Instruction[9]);
  not not_9 (not_9_out, Instruction[6]);
  not not_10 (not_10_out, Instruction[8]);
  not not_11 (not_11_out, Instruction[9]);
  not not_12 (not_12_out, Instruction[8]);
  not not_13 (not_13_out, Instruction[9]);
  not not_14 (not_14_out, Instruction[6]);
  not not_15 (not_15_out, Instruction[7]);
  not not_16 (not_16_out, Instruction[9]);
  flags flags_1 (
    .ANDS(ANDS), .EOR(EOR), .LSL(LSL), .LSR(LSR), .ASR(ASR), .RORS(RORS), .TST(TST), .ORR(ORR), .BIC(BIC),
    .MVN(MVN), .ADC(ADC), .SBC(SBC), .RSB(RSB), .CMP(CMP), .CMN(CMN), .MUL(MUL), .flag(res_flag));
  and and_2 (ANDS, not_2_out, not_3_out, not_4_out, not_5_out);
  and and_3 (EOR, Instruction[6], not_6_out, not_7_out, not_8_out);
  and and_4 (LSL, not_9_out, Instruction[7], not_10_out, not_11_out);
  and and_5 (LSR, Instruction[6], Instruction[7], not_12_out, not_13_out);
  and and_6 (ASR, not_14_out, not_15_out, Instruction[8], not_16_out);
  not not_17 (not_17_out, Instruction[9]);
  not not_18 (not_18_out, Instruction[6]);
  not not_19 (not_19_out, Instruction[7]);
  not not_20 (not_20_out, Instruction[8]);
  not not_21 (not_21_out, Instruction[6]);
  not not_22 (not_22_out, Instruction[7]);
  not not_23 (not_23_out, Instruction[6]);
  and and_7 (RORS, Instruction[6], Instruction[7], Instruction[8], not_17_out);
  and and_8 (TST, not_18_out, not_19_out, not_20_out, Instruction[9]);
  and and_9 (ORR, not_21_out, not_22_out, Instruction[8], Instruction[9]);
  and and_10 (BIC, not_23_out, Instruction[7], Instruction[8], Instruction[9]);
  and and_11 (MVN, Instruction[6], Instruction[7], Instruction[8], Instruction[9]);
  or or_1 (inv, MUL, RSB);
  Multiplexer #(.enable("false"), .width(3)) multiplexer_1 (
    .in0(3'b000), .in1(Instruction[5:3]), .out(rninv), .sel(inv));
  Multiplexer #(.enable("false"), .width(3)) multiplexer_2 (
    .in0(3'b000), .in1(Instruction[2:0]), .out(rminv), .sel(MUL));
  not not_24 (not_24_out, Instruction[7]);
  not not_25 (not_25_out, Instruction[9]);
  not not_26 (not_26_out, Instruction[6]);
  not not_27 (not_27_out, Instruction[9]);
  not not_28 (not_28_out, Instruction[7]);
  not not_29 (not_29_out, Instruction[8]);
  not not_30 (not_30_out, Instruction[6]);
  not not_31 (not_31_out, Instruction[8]);
  not not_32 (not_32_out, Instruction[8]);
  and and_12 (ADC, Instruction[6], not_24_out, Instruction[8], not_25_out);
  and and_13 (SBC, not_26_out, Instruction[7], Instruction[8], not_27_out);
  and and_14 (RSB, Instruction[6], not_28_out, not_29_out, Instruction[9]);
  and and_15 (CMP, not_30_out, Instruction[7], not_31_out, Instruction[9]);
  and and_16 (CMN, Instruction[6], Instruction[7], not_32_out, Instruction[9]);
  Multiplexer #(.enable("false"), .width(3)) multiplexer_3 (
    .in0(Instruction[2:0]), .in1(rninv), .out(multiplexer_3_out), .sel(inv));
  Multiplexer #(.enable("false"), .width(3)) multiplexer_4 (
    .in0(Instruction[5:3]), .in1(rminv), .out(multiplexer_4_out), .sel(MUL));
  Multiplexer #(.enable("false"), .width(4)) multiplexer_5 (
    .in0(4'b0000), .in1(Instruction[9:6]), .out(ALU_Opcode), .sel(Enable));
  Multiplexer #(.enable("false"), .width(4)) multiplexer_6 (
    .in0(4'b0000), .in1(res_flag), .out(Flags_Update_Mask), .sel(Enable));
  Multiplexer #(.enable("false"), .width(3)) multiplexer_7 (
    .in0(3'b000), .in1(Instruction[2:0]), .out(Rd), .sel(Enable));
  Multiplexer #(.enable("false"), .width(3)) multiplexer_8 (
    .in0(3'b000), .in1(multiplexer_3_out), .out(Rn), .sel(Enable));
  Multiplexer #(.enable("false"), .width(3)) multiplexer_9 (
    .in0(3'b000), .in1(multiplexer_4_out), .out(Rm), .sel(Enable));

  // Other names for the same wires on the sheet: en = Enable; b10 = Instruction[10]; b11 = Instruction[11];
  //   b12 = Instruction[12]; b13 = Instruction[13]; b14 = Instruction[14]; b15 = Instruction[15]; b6 = Instruction[6];
  //   opcode[3:0] = Instruction[9:6]; b7 = Instruction[7]; b8 = Instruction[8]; b9 = Instruction[9];
  //   b0 = Instruction[0]; rd_t[2:0] = Instruction[2:0]; rn_t[2:0] = Instruction[2:0]; b1 = Instruction[1];
  //   b2 = Instruction[2]; b3 = Instruction[3]; rm_t[2:0] = Instruction[5:3]; b4 = Instruction[4];
  //   b5 = Instruction[5]

  // Notes on the sheet:
  //   Pull output low on Enable = 0
  //   Note 2: RSB instruction has Rn as 1st operand.
  //   MUL instruction has Rn as 1st operand and Rdm as 2nd operand
  //   For simplification purposes, Rm is used for 1st operand both here and in the ALU.
  //   Note: instructions that does not save the result will still have the second operand as the destination register, the ALU will copy the second register to the destination register
endmodule

module flags (
  input  ANDS,
  input  EOR,
  input  LSL,
  input  LSR,
  input  ASR,
  input  RORS,
  input  TST,
  input  ORR,
  input  BIC,
  input  MVN,
  input  ADC,
  input  SBC,
  input  RSB,
  input  CMP,
  input  CMN,
  input  MUL,
  output [3:0] flag
);

  wire or_1_out, or_3_out;
  wire [3:0] res12, res14, res15;

  or or_1 (or_1_out, ANDS, EOR, LSL, LSR, ASR, RORS, TST, ORR, BIC, MVN);
  Multiplexer #(.enable("false"), .width(4)) multiplexer_1 (.in0(4'b0000), .in1(4'b1110), .out(res14), .sel(or_1_out));
  assign flag = res12 | res14 | res15;  // OR_Gate or_2, 4 bits wide
  Multiplexer #(.enable("false"), .width(4)) multiplexer_2 (.in0(4'b0000), .in1(4'b1100), .out(res12), .sel(MUL));
  or or_3 (or_3_out, ADC, SBC, RSB, CMP, CMN);
  Multiplexer #(.enable("false"), .width(4)) multiplexer_3 (.in0(4'b0000), .in1(4'b1111), .out(res15), .sel(or_3_out));
endmodule
