// Logisim project Ctl_Load_Store.circ as structural Verilog: 1 circuit, main circuit Load_Store
module Load_Store (
  input  Enable,
  input  [31:0] Stack_Pointer,
  input  [15:0] Instruction,
  input  Clk,
  input  Reset,
  output [31:0] RAM_Addr,
  output [2:0] Rmd,
  output Store,
  output Load,
  output PC_Hold
);

  wire and_1_out, d_ff_1_qn, not_1_out;
  wire [31:0] adder_1_out, bit_extender_1_out;

  and and_1 (and_1_out, Enable, Instruction[11], d_ff_1_qn);
  D_Flip_Flop d_ff_1 (.D(and_1_out), .clk(Clk), .Q(PC_Hold), .Qn(d_ff_1_qn), .reset(Reset));  // open: preset
  assign bit_extender_1_out = {{24{Instruction[7]}}, Instruction[7:0]};  // Bit_Extender bit_extender_1
  Multiplexer multiplexer_1 (.in0(1'b0), .in1(not_1_out), .out(Store), .sel(Enable));
  not not_1 (not_1_out, Instruction[11]);
  Adder #(.width(32)) adder_1 (.a(Stack_Pointer), .b(bit_extender_1_out), .out(adder_1_out));  // open: cin, cout
  Multiplexer #(.width(3)) multiplexer_2 (.in0(3'b000), .in1(Instruction[10:8]), .out(Rmd), .sel(Enable));
  Multiplexer multiplexer_3 (.in0(1'b0), .in1(Instruction[11]), .out(Load), .sel(Enable));
  Multiplexer #(.width(32)) multiplexer_4 (.in0({32{1'b0}}), .in1(adder_1_out), .out(RAM_Addr), .sel(Enable));

  // Other names for the same wires on the sheet: OpCode = Instruction[11]

  // Notes on the sheet:
  //   Instruction: pull=down
endmodule
