// Logisim project Ctl_Opcode_Decoder.circ as structural Verilog: 1 circuit, main circuit Opcode_Decoder
module Opcode_Decoder (
  input  [5:0] Opcode,
  output Shift,
  output Data_Processing,
  output Load_Store,
  output SP_Address,
  output Conditional
);

  wire and_5_out, and_6_out, not_1_out, not_2_out, not_3_out, not_4_out, not_5_out, not_6_out;

  not not_1 (not_1_out, Opcode[0]);
  not not_2 (not_2_out, Opcode[1]);
  not not_3 (not_3_out, Opcode[2]);
  not not_4 (not_4_out, Opcode[3]);
  not not_5 (not_5_out, Opcode[4]);
  not not_6 (not_6_out, Opcode[5]);
  and and_1 (Shift, not_5_out, not_6_out);
  and and_2 (Data_Processing, not_1_out, not_2_out, not_3_out, not_4_out, Opcode[4], not_6_out);
  and and_3 (Load_Store, Opcode[2], not_4_out, not_5_out, Opcode[5]);
  and and_4 (SP_Address, Opcode[2], Opcode[3], not_5_out, Opcode[5]);
  and and_5 (and_5_out, Opcode[2], not_4_out, Opcode[4], Opcode[5]);
  or or_1 (Conditional, and_5_out, and_6_out);
  and and_6 (and_6_out, not_2_out, not_3_out, Opcode[3], Opcode[4], Opcode[5]);

  // Notes on the sheet:
  //   Shift, add, sub, mov
  //   Load/Store
  //   SP Address
  //   Data Processing
  //   Conditional branch
endmodule
